# Fritzing sketch schematics (saved by Fritzing 0.9.3b)
breadboards: 1

parts:
  Part1 = Photon
  OLED_I2C1 = OLED 128x64 I2C Monochrome Display
  R1 = Resistor [tolerance=±5% resistance=2.2k package="2010 [SMD]"]
  R2 = Resistor [tolerance=±5% resistance=2.2k package="2010 [SMD]"]
  Part2 = Adafruit BME280

nets:
  GND: Part1.GND, OLED_I2C1.GND, R1.Pin_0, R2.Pin_0
  N1: Part1.D0, OLED_I2C1.SDA, R2.Pin_1, Part2.SDI/SDA
  N2: Part1.D1, OLED_I2C1.SCK, R1.Pin_1, Part2.SCK/SCL
  3V3: Part1.3V3, OLED_I2C1.VDD

custom parts:
  Adafruit BME280: Bosch has stepped up their game with their new BME280 sensor, an environmental sensor with temperature, barometric pressure and humidity! This sensor is great for all sorts of weather/environmental sensing and can even be used in both I2C and SPI! This precision sensor from Bosch is the best low-cost sensing solution for measuring humidity with ±3% accuracy, barometric pressure with ±1 hPa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
